# Fritzing sketch Blink (saved by Fritzing 0.9.3b)
breadboards: 1

parts:
  Part1 = Arduino Mega 2560 (Rev3)
  R1 = Resistor [tolerance=±5% resistance=330 package=THT]
  LED1 = smd LED [color="Red (633nm)" package="0603 [SMD]"]  # not connected

nets:
  N1: Part1.GND, R1.Pin_1
