# Fritzing sketch Bluetooth (saved by Fritzing 0.9.3b)
breadboards: 1

parts:
  Part1 = Bluetooth HC-05 Macho
  Part2 = Arduino Mega 2560 (Rev3)
  R4 = Resistor [tolerance=±5% resistance=1k package="2512 [SMD]"]
  R5 = Resistor [tolerance=±5% resistance=1k package="2512 [SMD]"]
  R6 = Resistor [tolerance=±5% resistance=1k package="2512 [SMD]"]

nets:
  N1: Part1.TXD, Part2.D19/RX1
  N2: Part1.RXD, R4.Pin_1, R5.Pin_1, R6.Pin_1
  VCC: Part1.VCC, Part2.5V
  GND: Part1.GND, Part2.GND, R5.Pin_0, R6.Pin_0
  N3: Part2.D18/TX1, R4.Pin_0
