# Fritzing sketch BluetoothLED (saved by Fritzing 0.9.6b)
breadboards: 1

parts:
  Part1 = Bluetooth HC-05 Macho
  Part2 = Arduino Mega 2560 (Rev3)
  R1 = Resistor [tolerance=±5% resistance=330 package="2512 [SMD]"]
  R2 = Resistor [tolerance=±5% resistance=330 package="2512 [SMD]"]
  R3 = Resistor [tolerance=±5% resistance=330 package="2512 [SMD]"]
  LED1 = smd LED [color="Red (633nm)" package="0603 [SMD]"]
  LED2 = smd LED [color="Green (570nm)" package="0603 [SMD]"]
  LED3 = smd LED [color="Red (633nm)" package="0805 [SMD]"]
  LED3_2 = smd LED [color="Blue (525nm)" package="1206 [SMD]"]
  R4 = Resistor [tolerance=±5% resistance=1k package="2512 [SMD]"]
  R5 = Resistor [tolerance=±5% resistance=1k package="2512 [SMD]"]
  R6 = Resistor [tolerance=±5% resistance=1k package="2512 [SMD]"]

nets:
  N1: Part1.TXD, Part2.D19/RX1
  N2: Part1.RXD, R4.Pin_1, R5.Pin_1, R6.Pin_1
  VCC: Part1.VCC, Part2.5V
  GND: Part1.GND, Part2.GND, R1.Pin_0, R2.Pin_0, R3.Pin_0, R5.Pin_0, R6.Pin_0
  N3: Part2.D18/TX1, R4.Pin_0
  N4: Part2.D2_PWM, LED1.anode
  N5: Part2.D3_PWM, LED2.anode
  N6: Part2.D4_PWM, LED3.anode, LED3_2.anode
  N7: R1.Pin_1, LED1.cathode
  N8: R2.Pin_1, LED2.cathode
  N9: R3.Pin_1, LED3.cathode, LED3_2.cathode
