# Fritzing sketch ButtonLED (saved by Fritzing 0.9.6b)
breadboards: 1

parts:
  Part1 = Arduino Mega 2560 (Rev3)
  R1 = Resistor [tolerance=±5% resistance=330 power=0.25 package=THT]
  LED1 = smd LED [color="Red (633nm)" package="0603 [SMD]"]
  S1 = Pushbutton [package="[THT]"]
  R2 = Resistor [tolerance=±5% resistance=10k power=0.25 package=THT]

nets:
  N1: Part1.GND, R1.Pin_1, R2.Pin_0
  N2: Part1.D13_PWM, LED1.anode
  N3: Part1.5V, S1.Pin_1, S1.Pin_2
  N4: Part1.D2_PWM, S1.Pin_3, S1.Pin_4, R2.Pin_1
  N5: R1.Pin_0, LED1.cathode
