# Fritzing sketch DHT11 (saved by Fritzing 0.9.3b)
breadboards: 1

parts:
  Part1 = Arduino Mega 2560 (Rev3)
  DHT1 = DHT11 Humitidy and Temperature Sensor

nets:
  5V: Part1.5V, DHT1.VDD
  N1: Part1.GND, DHT1.NULL

custom parts:
  DHT11 Humitidy and Temperature Sensor: DHT11 Humidity and Temperature Sensor
