# Fritzing sketch DisplayLCD (saved by Fritzing 0.9.3b)
breadboards: 1

parts:
  Part1 = Arduino Mega 2560 (Rev3)
  LCD1 = LCD screen
  U1 = POT [package=pot_alpha_rv16af-20]

nets:
  N1: Part1.D12_PWM, LCD1.RS
  N2: Part1.D11_PWM, LCD1.E
  5V: Part1.5V, LCD1.VDD, LCD1.LED+, U1.E
  GND: Part1.GND, LCD1.VSS, LCD1.R/W, LCD1.LED-, U1.A
  N3: Part1.D2_PWM, LCD1.DB7
  N4: Part1.D3_PWM, LCD1.DB6
  N5: Part1.D4_PWM, LCD1.DB5
  N6: Part1.D5_PWM, LCD1.DB4
  N7: LCD1.V0, U1.S
