# Fritzing sketch LDRWithThreeLEDS (saved by Fritzing 0.9.3b)
breadboards: 1

parts:
  Part1 = Arduino Mega 2560 (Rev3)
  R1 = Photocell (LDR) [package=THT]
  R2 = Resistor [tolerance=±5% resistance=10k package=THT]
  LED1 = LED - 5mm [color="Red (633nm)" package="5 mm [THT]"]
  LED2 = LED - 5mm [color="Red (633nm)" package="5 mm [THT]"]
  LED3 = LED - 5mm [color="Red (633nm)" package="5 mm [THT]"]
  R3 = Resistor [tolerance=±5% resistance=330 package=THT]
  R4 = Resistor [tolerance=±5% resistance=330 package=THT]
  R5 = Resistor [tolerance=±5% resistance=330 package=THT]

nets:
  N1: Part1.A0, R1.pin_0, R2.Pin_1
  N2: Part1.GND, R2.Pin_0, R3.Pin_0, R4.Pin_0, R5.Pin_0
  N3: Part1.D10_PWM, LED3.anode
  N4: Part1.D9_PWM, LED2.anode
  N5: Part1.D8_PWM, LED1.anode
  N6: Part1.5V, R1.pin_1
  N7: LED1.cathode, R5.Pin_1
  N8: LED2.cathode, R4.Pin_1
  N9: LED3.cathode, R3.Pin_1
