# Fritzing sketch PotentiometerLED (saved by Fritzing 0.9.6b)
breadboards: 1

parts:
  Part1 = Arduino Mega 2560 (Rev3)
  U1 = POT [package=pot_alpha_rv16af-20]
  LED1 = LED - 3mm [color="Red (633nm)" current=0.030 package="3 mm [THT]"]
  R1 = Resistor [tolerance=±5% resistance=220 package="0805 [SMD]"]

nets:
  N1: Part1.A0, U1.S
  N2: Part1.D9_PWM, LED1.anode
  N3: Part1.5V, U1.E
  N4: Part1.GND, U1.A, R1.Pin_1
  N5: LED1.cathode, R1.Pin_0
