# Fritzing sketch RFIDSensor-2 (saved by Fritzing 0.9.6b)
breadboards: 1

parts:
  Part1 = Arduino Mega 2560 (Rev3)
  Part2 = RFID-RC522-v2

nets:
  N1: Part1.D9_PWM, Part2.SDA
  N2: Part1.D8_PWM, Part2.RST
  3V3: Part1.3V3, Part2.3.3V
  GND: Part1.GND, Part2.GND
  N3: Part1.D50, Part2.MISO
  N4: Part1.D51, Part2.MOSI
  N5: Part1.D52, Part2.SCK

custom parts:
  RFID-RC522-v2: A simple China made RFID-RC522 Reader; do check the pin labels, as this is a MFRC522 based clone.
