# Fritzing sketch RFIDSensor (saved by Fritzing 0.9.3b)
breadboards: 1

parts:
  Part1 = Arduino Mega 2560 (Rev3)
  Part2 = RFID-RC522-v2

nets:
  N1: Part1.D13_PWM, Part2.SCK
  N2: Part1.D12_PWM, Part2.MISO
  N3: Part1.D11_PWM, Part2.MOSI
  N4: Part1.D9_PWM, Part2.RST
  N5: Part1.D8_PWM, Part2.SDA
  3V3: Part1.3V3, Part2.3.3V
  GND: Part1.GND, Part2.GND

custom parts:
  RFID-RC522-v2: A simple China made RFID-RC522 Reader; do check the pin labels, as this is a MFRC522 based clone.
