# Fritzing sketch Servo (saved by Fritzing 0.9.3b)

parts:
  Part1 = Arduino Mega 2560 (Rev3)
  SERVO1 = Tower Pro SG90 servo [part_number=101246]

nets:
  N1: Part1.D9_PWM, SERVO1.Signal
  5V: Part1.5V, SERVO1.+5V
  GND: Part1.GND, SERVO1.GND

custom parts:
  Tower Pro SG90 servo: Original file by John De Cristofaro http://www.adafruit.com/products/1449 Adafruit Feedback Servo (Small) Edited by: e-radionica.com 28/9/2015
