# Fritzing sketch ServoControl (saved by Fritzing 0.9.3b)
breadboards: 1

parts:
  SERVO1 = Tower Pro SG90 servo [part_number=101246]
  Part1 = Arduino Mega 2560 (Rev3)
  U1 = POT [package=pot_mammoth]

nets:
  N1: SERVO1.Signal, Part1.D9_PWM
  +5V: SERVO1.+5V, Part1.5V, U1.E
  N2: Part1.A0, U1.A
  N3: Part1.GND, U1.S

custom parts:
  Tower Pro SG90 servo: Original file by John De Cristofaro http://www.adafruit.com/products/1449 Adafruit Feedback Servo (Small) Edited by: e-radionica.com 28/9/2015
