# Fritzing sketch ServoPushButton (saved by Fritzing 0.9.3b)
breadboards: 1

parts:
  Part1 = Arduino Mega 2560 (Rev3)
  R1 = Resistor [tolerance=±5% resistance=10k package=THT]
  S1 = Pushbutton [package="[SMD]"]
  S2 = Pushbutton [package="[SMD]"]
  R2 = Resistor [tolerance=±5% resistance=10k package=THT]
  SERVO1 = Tower Pro SG90 servo [part_number=101246]

nets:
  GND: Part1.GND, R1.Pin_0, R2.Pin_0, SERVO1.GND
  N1: Part1.D9_PWM, SERVO1.Signal
  5V: Part1.5V, S1.Pin_1, S1.Pin_2, S2.Pin_1, S2.Pin_2, SERVO1.+5V
  N2: Part1.D2_PWM, R1.Pin_1, S1.Pin_3, S1.Pin_4
  N3: Part1.D3_PWM, S2.Pin_3, S2.Pin_4, R2.Pin_1

custom parts:
  Tower Pro SG90 servo: Original file by John De Cristofaro http://www.adafruit.com/products/1449 Adafruit Feedback Servo (Small) Edited by: e-radionica.com 28/9/2015
