# Fritzing sketch Ultrassonic (saved by Fritzing 0.9.3b)
breadboards: 1

parts:
  Part1 = Arduino Mega 2560 (Rev3)
  hc-sr1 = hc-sr04

nets:
  N1: Part1.D8_PWM, hc-sr1.GND
  N2: Part1.GND, hc-sr1.Trig
