# Fritzing sketch UltrassonicLEDs (saved by Fritzing 0.9.3b)
breadboards: 1

parts:
  Part1 = Arduino Mega 2560 (Rev3)
  hc-sr1 = hc-sr04
  LED1 = LED - 5mm [color="Red (633nm)" package="5 mm [THT]"]
  LED2 = LED - 5mm [color="Red (633nm)" package="5 mm [THT]"]
  R1 = Resistor [tolerance=±5% resistance=220 package=THT]
  R2 = Resistor [tolerance=±5% resistance=220 package=THT]

nets:
  N1: Part1.D13_PWM, LED2.cathode
  N2: Part1.D12_PWM, LED1.cathode
  N3: Part1.D8_PWM, hc-sr1.Trig
  5V: Part1.5V, hc-sr1.VCC
  GND: Part1.GND, hc-sr1.GND, R1.Pin_1, R2.Pin_1
  N4: Part1.D7_PWM, hc-sr1.Echo
  N5: LED1.anode, R2.Pin_0
  N6: LED2.anode, R1.Pin_0
