# Fritzing sketch UltrassonicServo (saved by Fritzing 0.9.3b)
breadboards: 1

parts:
  Part1 = Arduino Mega 2560 (Rev3)
  hc-sr1 = hc-sr04
  SERVO2 = Tower Pro SG90 servo [part_number=101246]

nets:
  N1: Part1.D9_PWM, hc-sr1.GND
  5V: Part1.5V, SERVO2.+5V
  GND: Part1.GND, hc-sr1.Trig, SERVO2.GND
  N2: Part1.D6_PWM, SERVO2.Signal

custom parts:
  Tower Pro SG90 servo: Original file by John De Cristofaro http://www.adafruit.com/products/1449 Adafruit Feedback Servo (Small) Edited by: e-radionica.com 28/9/2015
