# Fritzing sketch WiFiLED (saved by Fritzing 0.9.3b)
breadboards: 1

parts:
  ESP8266_Shield1 = WangTongze ESP8266 WiFi Shield - Debug Port
  LED1 = smd LED [color="Blue (525nm)" package="0603 [SMD]"]
  R1 = Resistor [tolerance=±5% resistance=330 package="0603 [SMD]"]
  Part1 = Arduino Mega 2560 (Rev3)

nets:
  N1: ESP8266_Shield1.TXD, Part1.D19/RX1
  N2: ESP8266_Shield1.RXD, Part1.D18/TX1
  5V: ESP8266_Shield1.5V, Part1.5V
  GND: ESP8266_Shield1.GND, R1.Pin_0, Part1.GND
  N3: LED1.anode, Part1.D13_PWM

custom parts:
  WangTongze ESP8266 WiFi Shield - Debug Port: Basic teaching part focused on the five-pin Debug Port.
