# Fritzing sketch WiFiServo (saved by Fritzing 0.9.3b)
breadboards: 1

parts:
  ESP8266_Shield1 = WangTongze ESP8266 WiFi Shield - Debug Port
  Part1 = Arduino Mega 2560 (Rev3)
  SERVO2 = Tower Pro SG90 servo [part_number=101246]

nets:
  N1: ESP8266_Shield1.TXD, Part1.D19/RX1
  N2: ESP8266_Shield1.RXD, Part1.D18/TX1
  5V: ESP8266_Shield1.5V, Part1.5V, SERVO2.+5V
  GND: ESP8266_Shield1.GND, Part1.GND, SERVO2.GND
  N3: Part1.D9_PWM, SERVO2.Signal

custom parts:
  WangTongze ESP8266 WiFi Shield - Debug Port: Basic teaching part focused on the five-pin Debug Port.
  Tower Pro SG90 servo: Original file by John De Cristofaro http://www.adafruit.com/products/1449 Adafruit Feedback Servo (Small) Edited by: e-radionica.com 28/9/2015
